# Fritzing sketch wiring (saved by Fritzing 0.9.3b)
breadboards: 1

parts:
  U1 = NodeMCU V1.0
  R1 = Resistor [tolerance=±5% resistance=220 package="0603 [SMD]"]
  Part1 = LCD1602-I2C
  DS1 = DS18B20 1-Wire Temperature Sensor [part_number=DS18B20]

nets:
  N1: U1.D3, R1.Pin_1, DS1.DQ
  N2: U1.D4, Part1.SDA
  3V3: U1.3V3, R1.Pin_0, DS1.VDD
  GND: U1.GND, Part1.GND, DS1.GND
  N3: U1.D5, Part1.SCL
  VIN: U1.Vin, Part1.VCC

custom parts:
  NodeMCU V1.0: ESP8266 based NodeMCU
  LCD1602-I2C: A standard character display, usually with 2x16 characters. Comes in many colors with LCM1602 IIC attached.
